// Logisim project 16Bit_CPU.circ as structural Verilog: 6 circuits, main circuit  Register
module Register (
  input  CLK,
  input  Enable,
  input  Load,
  input  [15:0] Bus_In,
  input  in_5,
  output [15:0] out_6,
  output [15:0] Bus_Out
);

  wire not_1_out;

  BusTransciever bustransciever_1 (.Enable(Enable), .Direction(1'b0), .BusA(Bus_Out), .BusB(out_6));
  not not_1 (not_1_out, Load);
  // Probe on out_6
  Register_part #(.width(4)) register_1 (.D(Bus_In[3:0]), .en(not_1_out), .Q(out_6[3:0]), .clk(CLK), .clr(in_5));
  Register_part #(.width(4)) register_2 (.D(Bus_In[7:4]), .en(not_1_out), .Q(out_6[7:4]), .clk(CLK), .clr(in_5));
  Register_part #(.width(4)) register_3 (.D(Bus_In[11:8]), .en(not_1_out), .Q(out_6[11:8]), .clk(CLK), .clr(in_5));
  Register_part #(.width(4)) register_4 (.D(Bus_In[15:12]), .en(not_1_out), .Q(out_6[15:12]), .clk(CLK), .clr(in_5));
endmodule

module BusTransciever (
  input  Enable,
  input  Direction,
  input  [15:0] BusB,
  output [15:0] BusA
);

  wire and_1_out, and_2_out;

  // Probe on BusA
  and and_1 (and_1_out, ~Enable, ~Direction);  // AND_Gate
  and and_2 (and_2_out, ~Enable, Direction);  // AND_Gate
  assign BusA[1] = and_1_out ? BusB[1] : 1'bz;  // Controlled_Buffer controlled_buffer_1
  assign BusA[0] = and_1_out ? BusB[0] : 1'bz;  // Controlled_Buffer controlled_buffer_2
  assign BusB[1] = and_2_out ? BusA[1] : 1'bz;  // Controlled_Buffer controlled_buffer_3
  assign BusB[0] = and_2_out ? BusA[0] : 1'bz;  // Controlled_Buffer controlled_buffer_4
  assign BusA[2] = and_1_out ? BusB[2] : 1'bz;  // Controlled_Buffer controlled_buffer_5
  assign BusA[3] = and_1_out ? BusB[3] : 1'bz;  // Controlled_Buffer controlled_buffer_6
  assign BusB[3] = and_2_out ? BusA[3] : 1'bz;  // Controlled_Buffer controlled_buffer_7
  assign BusB[2] = and_2_out ? BusA[2] : 1'bz;  // Controlled_Buffer controlled_buffer_8
  assign BusA[4] = and_1_out ? BusB[4] : 1'bz;  // Controlled_Buffer controlled_buffer_9
  assign BusA[5] = and_1_out ? BusB[5] : 1'bz;  // Controlled_Buffer controlled_buffer_10
  assign BusB[4] = and_2_out ? BusA[4] : 1'bz;  // Controlled_Buffer controlled_buffer_11
  assign BusB[5] = and_2_out ? BusA[5] : 1'bz;  // Controlled_Buffer controlled_buffer_12
  assign BusA[7] = and_1_out ? BusB[7] : 1'bz;  // Controlled_Buffer controlled_buffer_13
  assign BusA[6] = and_1_out ? BusB[6] : 1'bz;  // Controlled_Buffer controlled_buffer_14
  assign BusB[6] = and_2_out ? BusA[6] : 1'bz;  // Controlled_Buffer controlled_buffer_15
  assign BusB[7] = and_2_out ? BusA[7] : 1'bz;  // Controlled_Buffer controlled_buffer_16
  assign BusA[9] = and_1_out ? BusB[9] : 1'bz;  // Controlled_Buffer controlled_buffer_17
  assign BusA[8] = and_1_out ? BusB[8] : 1'bz;  // Controlled_Buffer controlled_buffer_18
  assign BusB[9] = and_2_out ? BusA[9] : 1'bz;  // Controlled_Buffer controlled_buffer_19
  assign BusB[8] = and_2_out ? BusA[8] : 1'bz;  // Controlled_Buffer controlled_buffer_20
  assign BusA[11] = and_1_out ? BusB[11] : 1'bz;  // Controlled_Buffer controlled_buffer_21
  assign BusA[10] = and_1_out ? BusB[10] : 1'bz;  // Controlled_Buffer controlled_buffer_22
  assign BusB[10] = and_2_out ? BusA[10] : 1'bz;  // Controlled_Buffer controlled_buffer_23
  assign BusB[11] = and_2_out ? BusA[11] : 1'bz;  // Controlled_Buffer controlled_buffer_24
  assign BusA[12] = and_1_out ? BusB[12] : 1'bz;  // Controlled_Buffer controlled_buffer_25
  assign BusA[13] = and_1_out ? BusB[13] : 1'bz;  // Controlled_Buffer controlled_buffer_26
  assign BusB[12] = and_2_out ? BusA[12] : 1'bz;  // Controlled_Buffer controlled_buffer_27
  assign BusB[13] = and_2_out ? BusA[13] : 1'bz;  // Controlled_Buffer controlled_buffer_28
  assign BusA[14] = and_1_out ? BusB[14] : 1'bz;  // Controlled_Buffer controlled_buffer_29
  assign BusA[15] = and_1_out ? BusB[15] : 1'bz;  // Controlled_Buffer controlled_buffer_30
  assign BusB[15] = and_2_out ? BusA[15] : 1'bz;  // Controlled_Buffer controlled_buffer_31
  assign BusB[14] = and_2_out ? BusA[14] : 1'bz;  // Controlled_Buffer controlled_buffer_32
  // Probe on BusB
endmodule

module main (
  input  in_1,
  input  in_2,
  input  in_3,
  input  in_4,
  input  in_5,
  input  in_6,
  input  in_7,
  input  in_8,
  input  in_9,
  input  in_10,
  input  in_11,
  input  in_12,
  input  in_13,
  input  [15:0] in_14
);

  wire alu_1_carry_flag, clock_1_out, clock_2_out, clock_3_out;
  wire [7:0] instr_register_1_out_6;
  wire [15:0] A_out_6, B_out_6, instr_register_1_out_5, pull_resistor_13_node;

  Instr_Register instr_register_1 (
    .in_1(clock_1_out), .in_2(in_1), .in_3(in_2), .in_4(pull_resistor_13_node),
    .out_5(instr_register_1_out_5), .out_6(instr_register_1_out_6));
  Clock clock_1 (.out(clock_1_out));
  // NAND_Gate nand_1 has open pins: in0=in_4, in1=in_5, in2=in_7, in3=in_12, out=open
  // NAND_Gate nand_2 has open pins: in0=in_4, in1=in_5, in2=in_7, in3=in_12, out=open
  // NAND_Gate nand_3 has open pins: in0=in_4, in1=in_5, in2=in_7, in3=in_12, out=open
  // NAND_Gate nand_4 has open pins: in0=in_4, in1=in_5, in2=in_7, in3=in_12, out=open
  LED led_1 (.in(pull_resistor_13_node[15]));
  // Probe on instr_register_1_out_5
  // Probe on instr_register_1_out_6
  LED led_2 (.in(pull_resistor_13_node[14]));
  LED led_3 (.in(pull_resistor_13_node[11]));
  LED led_4 (.in(pull_resistor_13_node[12]));
  LED led_5 (.in(pull_resistor_13_node[13]));
  Pull_Resistor pull_resistor_1 (.node(pull_resistor_13_node[15]));
  LED led_6 (.in(pull_resistor_13_node[7]));
  LED led_7 (.in(pull_resistor_13_node[10]));
  LED led_8 (.in(pull_resistor_13_node[8]));
  LED led_9 (.in(pull_resistor_13_node[9]));
  Pull_Resistor pull_resistor_2 (.node(pull_resistor_13_node[13]));
  Pull_Resistor pull_resistor_3 (.node(pull_resistor_13_node[8]));
  Pull_Resistor pull_resistor_4 (.node(pull_resistor_13_node[12]));
  Pull_Resistor pull_resistor_5 (.node(pull_resistor_13_node[14]));
  Pull_Resistor pull_resistor_6 (.node(pull_resistor_13_node[9]));
  Pull_Resistor pull_resistor_7 (.node(pull_resistor_13_node[7]));
  Pull_Resistor pull_resistor_8 (.node(pull_resistor_13_node[11]));
  Pull_Resistor pull_resistor_9 (.node(pull_resistor_13_node[10]));
  // Probe on pull_resistor_13_node
  LED led_10 (.in(pull_resistor_13_node[3]));
  LED led_11 (.in(pull_resistor_13_node[6]));
  LED led_12 (.in(pull_resistor_13_node[5]));
  LED led_13 (.in(pull_resistor_13_node[4]));
  Pull_Resistor pull_resistor_10 (.node(pull_resistor_13_node[3]));
  Pull_Resistor pull_resistor_11 (.node(pull_resistor_13_node[4]));
  Pull_Resistor pull_resistor_12 (.node(pull_resistor_13_node[6]));
  Pull_Resistor pull_resistor_13 (.node(pull_resistor_13_node[0]));
  Pull_Resistor pull_resistor_14 (.node(pull_resistor_13_node[2]));
  Pull_Resistor pull_resistor_15 (.node(pull_resistor_13_node[5]));
  Pull_Resistor pull_resistor_16 (.node(pull_resistor_13_node[1]));
  // Probe on pull_resistor_13_node
  // Probe on pull_resistor_13_node
  LED led_14 (.in(pull_resistor_13_node[1]));
  LED led_15 (.in(pull_resistor_13_node[0]));
  LED led_16 (.in(pull_resistor_13_node[2]));
  Clock clock_2 (.out(clock_2_out));
  Register A (
    .CLK(clock_2_out), .Enable(in_6), .Load(in_3), .Bus_Out(pull_resistor_13_node),
    .Bus_In(pull_resistor_13_node), .out_6(A_out_6));  // open: in_5
  Clock clock_3 (.out(clock_3_out));
  Register B (
    .CLK(clock_3_out), .Enable(in_9), .Load(in_13), .Bus_Out(pull_resistor_13_node),
    .Bus_In(pull_resistor_13_node), .out_6(B_out_6));  // open: in_5
  ALU alu_1 (
    .ALU_Output(in_8), .Bus_connect(pull_resistor_13_node), .Subtract(in_11), .A_Reg(A_out_6),
    .B_Reg(B_out_6), .carry_flag(alu_1_carry_flag));
  LED led_17 (.in(alu_1_carry_flag));
  BusTransciever bustransciever_1 (.Enable(in_10), .Direction(1'b0), .BusA(pull_resistor_13_node), .BusB(in_14));

  // Notes on the sheet:
  //   BUS
  //   Input_Section
endmodule

module ALU (
  input  ALU_Output,
  input  Subtract,
  input  [15:0] A_Reg,
  input  [15:0] B_Reg,
  output [15:0] Bus_connect,
  output carry_flag
);

  wire adder_1_cout, adder_2_cout, adder_3_cout;
  wire [3:0] adder_1_out, adder_2_out, adder_3_out, adder_4_out;
  wire [15:0] xor_1_out;

  BusTransciever bustransciever_1 (
    .Enable(ALU_Output), .Direction(1'b0), .BusA(Bus_connect),
    .BusB({adder_4_out, adder_3_out, adder_2_out, adder_1_out}));
  xor xor_1 (xor_1_out[0], Subtract, B_Reg[0]);
  xor xor_2 (xor_1_out[1], Subtract, B_Reg[1]);
  xor xor_3 (xor_1_out[2], Subtract, B_Reg[2]);
  xor xor_4 (xor_1_out[3], Subtract, B_Reg[3]);
  xor xor_5 (xor_1_out[4], Subtract, B_Reg[4]);
  xor xor_6 (xor_1_out[5], Subtract, B_Reg[5]);
  xor xor_7 (xor_1_out[6], Subtract, B_Reg[6]);
  xor xor_8 (xor_1_out[7], Subtract, B_Reg[7]);
  xor xor_9 (xor_1_out[8], Subtract, B_Reg[8]);
  xor xor_10 (xor_1_out[9], Subtract, B_Reg[9]);
  xor xor_11 (xor_1_out[10], Subtract, B_Reg[10]);
  xor xor_12 (xor_1_out[11], Subtract, B_Reg[11]);
  xor xor_13 (xor_1_out[12], Subtract, B_Reg[12]);
  xor xor_14 (xor_1_out[13], Subtract, B_Reg[13]);
  xor xor_15 (xor_1_out[14], Subtract, B_Reg[14]);
  xor xor_16 (xor_1_out[15], Subtract, B_Reg[15]);
  Adder #(.width(4)) adder_1 (
    .a(A_Reg[3:0]), .b(xor_1_out[3:0]), .out(adder_1_out), .cin(Subtract), .cout(adder_1_cout));
  Adder #(.width(4)) adder_2 (
    .a(A_Reg[7:4]), .b(xor_1_out[7:4]), .out(adder_2_out), .cin(adder_1_cout), .cout(adder_2_cout));
  Adder #(.width(4)) adder_3 (
    .a(A_Reg[11:8]), .b(xor_1_out[11:8]), .out(adder_3_out), .cin(adder_2_cout), .cout(adder_3_cout));
  Adder #(.width(4)) adder_4 (
    .a(A_Reg[15:12]), .b(xor_1_out[15:12]), .out(adder_4_out), .cin(adder_3_cout), .cout(carry_flag));
endmodule

module Instr_Register (
  input  in_1,
  input  in_2,
  input  in_3,
  input  [15:0] in_4,
  output [15:0] out_5,
  output [7:0] out_6
);

  wire [7:0] register_1_bus_out;

  BusTransciever bustransciever_1 (
    .Enable(in_2), .Direction(1'b0), .BusA(out_5), .BusB({{8{1'b0}}, register_1_bus_out}));
  Register register_1 (
    .CLK(in_1), .Enable(in_2), .Load(in_3), .Bus_Out({out_6, register_1_bus_out}), .Bus_In(in_4));  // open: in_5, out_6
endmodule

module RAM (
  input  in_1,
  input  in_2,
  input  in_3,
  output [15:0] out_4
);

  wire [7:0] ram_1_data, ram_2_data, undriven_2, undriven_3;
  wire [15:0] undriven;

  BusTransciever bustransciever_1 (.Enable(in_1), .Direction(1'b0), .BusA(out_4), .BusB(undriven));
  RAM_part #(.addrWidth(15), .bus("asynch")) ram_1 (
    .addr({{7{1'b0}}, undriven_2}), .data(ram_1_data), .sel(1'b1), .ld(in_3), .clr(in_2));
  RAM_part #(.addrWidth(15), .bus("asynch")) ram_2 (
    .addr({{7{1'b0}}, undriven_3}), .data(ram_2_data), .sel(1'b1), .ld(in_3), .clr(in_2));
endmodule
