// Logisim project 8Bit_CPU.circ as structural Verilog: 7 circuits, main circuit main
module main (
  input  in_1,
  input  in_2,
  input  in_3,
  input  in_4,
  input  in_5,
  input  [3:0] in_6,
  input  in_7,
  input  in_8,
  input  in_9,
  input  in_10,
  input  [7:0] in_11
);

  wire alu_1_carry_out, and_1_out, Clock_out;
  wire [3:0] ram_1_value_output, ram_1_value_output_2;
  wire [7:0] register_1_constant_out, register_2_constant_out;

  LED led_1 (.in(Clock_out));
  Clock Clock (.out(Clock_out));
  LED led_2 (.in(and_1_out));
  buf and_1 (and_1_out, Clock_out);  // AND_Gate AND_Gate
  RAM ram_1 (
    .Addr_Input(in_6), .Value_Output({ram_1_value_output_2, ram_1_value_output}),
    .Value_Input({ram_1_value_output_2, ram_1_value_output}), .Enable_Output(in_4), .CLK(and_1_out),
    .Enable_Input(in_8));
  Hex_Digit_Display hex_digit_display_1 (.value(ram_1_value_output_2));  // open: dp
  Hex_Digit_Display hex_digit_display_2 (.value(ram_1_value_output));  // open: dp
  LED led_3 (.in(ram_1_value_output_2[1]));
  LED led_4 (.in(ram_1_value_output_2[3]));
  LED led_5 (.in(ram_1_value_output_2[0]));
  LED led_6 (.in(ram_1_value_output_2[2]));
  Pull_Resistor pull_resistor_1 (.node(ram_1_value_output_2[3]));
  Pull_Resistor pull_resistor_2 (.node(ram_1_value_output_2[2]));
  Pull_Resistor pull_resistor_3 (.node(ram_1_value_output_2[0]));
  Pull_Resistor pull_resistor_4 (.node(ram_1_value_output_2[1]));
  Pull_Resistor pull_resistor_5 (.node(ram_1_value_output[3]));
  LED led_7 (.in(ram_1_value_output[3]));
  LED led_8 (.in(ram_1_value_output[2]));
  LED led_9 (.in(ram_1_value_output[0]));
  LED led_10 (.in(ram_1_value_output[1]));
  Pull_Resistor pull_resistor_6 (.node(ram_1_value_output[1]));
  Pull_Resistor pull_resistor_7 (.node(ram_1_value_output[2]));
  Pull_Resistor pull_resistor_8 (.node(ram_1_value_output[0]));
  Register register_1 (
    .Clk(and_1_out), .Load(in_1), .Bus_In({ram_1_value_output_2, ram_1_value_output}),
    .Bus_Out({ram_1_value_output_2, ram_1_value_output}), .Out_Enable(in_2),
    .Constant_Out(register_1_constant_out));
  ALU alu_1 (
    .B_Register(register_2_constant_out), .A_Register(register_1_constant_out),
    .Bus_Out({ram_1_value_output_2, ram_1_value_output}), .Substract(in_5), .Enable_Output(in_3),
    .Carry_Out(alu_1_carry_out));
  Register register_2 (
    .Clk(and_1_out), .Load(in_7), .Bus_In({ram_1_value_output_2, ram_1_value_output}),
    .Bus_Out({ram_1_value_output_2, ram_1_value_output}), .Out_Enable(in_10),
    .Constant_Out(register_2_constant_out));
  Hex_Digit_Display hex_digit_display_3 (.value(register_1_constant_out[7:4]));  // open: dp
  Hex_Digit_Display hex_digit_display_4 (.value(register_2_constant_out[7:4]));  // open: dp
  Bus_Interface bus_interface_1 (
    .Enable(in_9), .Input(in_11[0]), .Input_2(in_11[1]), .Input_3(in_11[2]), .Input_4(in_11[3]),
    .Input_5(in_11[4]), .Input_6(in_11[5]), .Input_7(in_11[6]), .Input_8(in_11[7]),
    .Output(ram_1_value_output[0]), .Output_2(ram_1_value_output[1]), .Output_3(ram_1_value_output[2]),
    .Output_4(ram_1_value_output[3]), .Output_5(ram_1_value_output_2[0]), .Output_6(ram_1_value_output_2[1]),
    .Output_7(ram_1_value_output_2[2]), .Output_8(ram_1_value_output_2[3]));
  Hex_Digit_Display hex_digit_display_5 (.value(register_1_constant_out[3:0]));  // open: dp
  Hex_Digit_Display hex_digit_display_6 (.value(register_2_constant_out[3:0]));  // open: dp
  LED led_11 (.in(alu_1_carry_out));
endmodule

module SR_latch (
  input  in_1,
  input  in_2,
  output out_3,
  output out_4
);

  nor nor_1 (out_3, in_1, out_4);
  nor nor_2 (out_4, out_3, in_2);
endmodule

module Bus_Interface (
  input  Enable,
  input  Input,
  input  Input_2,
  input  Input_3,
  input  Input_4,
  input  Input_5,
  input  Input_6,
  input  Input_7,
  input  Input_8,
  output Output,
  output Output_2,
  output Output_3,
  output Output_4,
  output Output_5,
  output Output_6,
  output Output_7,
  output Output_8
);

  assign Output = Enable ? Input : 1'bz;  // Controlled_Buffer controlled_buffer_1
  assign Output_2 = Enable ? Input_2 : 1'bz;  // Controlled_Buffer controlled_buffer_2
  assign Output_3 = Enable ? Input_3 : 1'bz;  // Controlled_Buffer controlled_buffer_3
  assign Output_4 = Enable ? Input_4 : 1'bz;  // Controlled_Buffer controlled_buffer_4
  assign Output_5 = Enable ? Input_5 : 1'bz;  // Controlled_Buffer controlled_buffer_5
  assign Output_6 = Enable ? Input_6 : 1'bz;  // Controlled_Buffer controlled_buffer_6
  assign Output_7 = Enable ? Input_7 : 1'bz;  // Controlled_Buffer controlled_buffer_7
  assign Output_8 = Enable ? Input_8 : 1'bz;  // Controlled_Buffer controlled_buffer_8
endmodule

module Register (
  input  Clk,
  input  Load,
  input  [7:0] Bus_In,
  input  Out_Enable,
  output [7:0] Bus_Out,
  output [7:0] Constant_Out
);

  wire button_1_out, not_1_out;

  not not_1 (not_1_out, Load);
  Bus_Interface bus_interface_1 (
    .Enable(Out_Enable), .Input(Constant_Out[7]), .Input_2(Constant_Out[6]), .Input_3(Constant_Out[5]),
    .Input_4(Constant_Out[4]), .Input_5(Constant_Out[3]), .Input_6(Constant_Out[2]),
    .Input_7(Constant_Out[1]), .Input_8(Constant_Out[0]), .Output(Bus_Out[7]), .Output_2(Bus_Out[6]),
    .Output_3(Bus_Out[5]), .Output_4(Bus_Out[4]), .Output_5(Bus_Out[3]), .Output_6(Bus_Out[2]),
    .Output_7(Bus_Out[1]), .Output_8(Bus_Out[0]));
  Register_part #(.width(4)) register_1 (
    .D(Bus_In[3:0]), .en(not_1_out), .Q(Constant_Out[3:0]), .clk(Clk), .clr(button_1_out));
  Register_part #(.width(4)) register_2 (
    .D(Bus_In[7:4]), .en(not_1_out), .Q(Constant_Out[7:4]), .clk(Clk), .clr(button_1_out));
  Button button_1 (.out(button_1_out));
endmodule

module ALU (
  input  [7:0] A_Register,
  input  Enable_Output,
  input  Substract,
  input  [7:0] B_Register,
  output [7:0] Bus_Out,
  output Carry_Out
);

  wire adder_1_cout;
  wire [7:0] adder_1_out, substraction_engine_1_out_3;

  Bus_Interface bus_interface_1 (
    .Enable(Enable_Output), .Input(adder_1_out[0]), .Input_2(adder_1_out[1]), .Input_3(adder_1_out[2]),
    .Input_4(adder_1_out[3]), .Input_5(adder_1_out[4]), .Input_6(adder_1_out[5]), .Input_7(adder_1_out[6]),
    .Input_8(adder_1_out[7]), .Output(Bus_Out[0]), .Output_2(Bus_Out[1]), .Output_3(Bus_Out[2]),
    .Output_4(Bus_Out[3]), .Output_5(Bus_Out[4]), .Output_6(Bus_Out[5]), .Output_7(Bus_Out[6]),
    .Output_8(Bus_Out[7]));
  Substraction_Engine substraction_engine_1 (.in_1(Substract), .in_2(B_Register), .out_3(substraction_engine_1_out_3));
  Adder #(.width(4)) adder_1 (
    .a(A_Register[3:0]), .b(substraction_engine_1_out_3[3:0]), .out(adder_1_out[3:0]), .cin(Substract),
    .cout(adder_1_cout));
  Adder #(.width(4)) adder_2 (
    .a(A_Register[7:4]), .b(substraction_engine_1_out_3[7:4]), .out(adder_1_out[7:4]), .cin(adder_1_cout),
    .cout(Carry_Out));
endmodule

module Substraction_Engine (
  input  in_1,
  input  [7:0] in_2,
  output [7:0] out_3
);

  buf xor_1 (out_3[0], in_1);  // XOR_Gate
  xor xor_2 (out_3[1], in_1, in_2[1]);
  xor xor_3 (out_3[2], in_1, in_2[2]);
  xor xor_4 (out_3[3], in_1, in_2[3]);
  xor xor_5 (out_3[4], in_1, in_2[4]);
  xor xor_6 (out_3[5], in_1, in_2[5]);
  xor xor_7 (out_3[6], in_1, in_2[6]);
  xor xor_8 (out_3[7], in_1, in_2[7]);
endmodule

module RAM (
  input  Enable_Output,
  input  [3:0] Addr_Input,
  input  [7:0] Value_Input,
  input  Enable_Input,
  input  CLK,
  output [7:0] Value_Output
);

  wire pull_resistor_1_node;
  wire [7:0] ram_1_data;

  RAM_part #(.addrWidth(4)) ram_1 (
    .addr(Addr_Input), .data(ram_1_data), .sel(1'b1), .clk(CLK), .ld(pull_resistor_1_node), .clr(1'b0));
  Pull_Resistor #(.pull(1)) pull_resistor_1 (.node(pull_resistor_1_node));
  not not_1 (pull_resistor_1_node, Enable_Input);
  Bus_Interface bus_interface_1 (
    .Enable(Enable_Output), .Input(ram_1_data[0]), .Input_2(ram_1_data[1]), .Input_3(ram_1_data[2]),
    .Input_4(ram_1_data[3]), .Input_5(ram_1_data[4]), .Input_6(ram_1_data[5]), .Input_7(ram_1_data[6]),
    .Input_8(ram_1_data[7]), .Output(Value_Output[0]), .Output_2(Value_Output[1]),
    .Output_3(Value_Output[2]), .Output_4(Value_Output[3]), .Output_5(Value_Output[4]),
    .Output_6(Value_Output[5]), .Output_7(Value_Output[6]), .Output_8(Value_Output[7]));
  Bus_Interface bus_interface_2 (
    .Enable(Enable_Input), .Input(Value_Input[7]), .Input_2(Value_Input[6]), .Input_3(Value_Input[5]),
    .Input_4(Value_Input[4]), .Input_5(Value_Input[3]), .Input_6(Value_Input[2]), .Input_7(Value_Input[1]),
    .Input_8(Value_Input[0]), .Output(ram_1_data[7]), .Output_2(ram_1_data[6]), .Output_3(ram_1_data[5]),
    .Output_4(ram_1_data[4]), .Output_5(ram_1_data[3]), .Output_6(ram_1_data[2]), .Output_7(ram_1_data[1]),
    .Output_8(ram_1_data[0]));
endmodule
